// Digital circuit cache.dig as structural Verilog
module cache (
  input  [15:0] LD_instr,
  input  [15:0] D_RAM,
  input  C,
  output [5:0] addr,
  output ld,
  output [15:0] D_o
);

  wire decoder_1_out_0;
  wire [8:0] demultiplexer_1_out_0;
  wire [8:6] demultiplexer_1_out_1;
  wire [15:0] multiplexer_1_out;

  // Probe on LD_instr[3:1]
  Decoder decoder_1 (.sel(LD_instr[6]), .out_0(decoder_1_out_0), .out_1(ld));
  // Probe on decoder_1_out_0
  Demultiplexer #(.Bits(9)) demultiplexer_1 (
    .sel(LD_instr[6]), .in(LD_instr[15:7]), .out_0(demultiplexer_1_out_0),
    .out_1({demultiplexer_1_out_1, addr}));
  Multiplexer #(.Bits(16)) multiplexer_1 (
    .sel(LD_instr[6]), .in_0({{7{1'b0}}, demultiplexer_1_out_0}), .in_1(D_RAM), .out(multiplexer_1_out));
  // regfile regfile_1: pin names not known; wires that end beside it: LD_instr[0], LD_instr[5:4], LD_instr[5:4], multiplexer_1_out, C, D_o
endmodule
