// Digital circuit fetch.dig as structural Verilog
module fetch (
  input  C,
  output error,
  output halt,
  output [15:0] D_o
);

  wire alu_1_en, C_t, decoder_1_out_0, decoder_2_p3, err, ld_en, load, st_en, store;
  wire [1:0] alu_1_rd, alu_1_rs_1, priorityencoder_1_num;
  wire [5:0] _1A, PC_out;
  wire [15:0] add, alu_1_d_res, D_in, halt_t, IR_q, ramdualaccess_1_d1, ramdualaccess_1_d2;

  PriorityEncoder #(.Selector_Bits(2)) priorityencoder_1 (
    .in0(1'b1), .in1(halt_t[0]), .in2(err), .in3(1'b0), .num(priorityencoder_1_num));  // open: any
  Counter #(.Bits(6)) PC (.en(1'b1), .C(C_t), .clr(1'b0), .out(PC_out), .ovf(err));
  Decoder #(.Selector_Bits(2)) decoder_1 (
    .sel(priorityencoder_1_num), .out_0(decoder_1_out_0), .out_1(halt), .out_2(error));  // open: out_3
  alu alu_1 (
    .ADD_instr(add), .D_cache(D_o), .rs_1(alu_1_rs_1), .D_res(alu_1_d_res), .rd(alu_1_rd), .en(alu_1_en),
    .ovf(err));
  and and_1 (C_t, C, decoder_1_out_0);
  RAMDualAccess #(.AddrBits(6), .isProgramMemory("true"), .Bits(16)) ramdualaccess_1 (
    .str(st_en), .C(C_t), .ld(ld_en), .A1(_1A), .Din1(D_in), .A2(PC_out), .D1(ramdualaccess_1_d1),
    .D2(ramdualaccess_1_d2));
  // cache cache_1: pin names not known; wires that end beside it: load, ramdualaccess_1_d1, C_t, store, alu_1_rs_1, alu_1_d_res, alu_1_rd, alu_1_en, _1A, ld_en, D_o, st_en, D_in
  Register #(.Bits(16)) IR (.D(ramdualaccess_1_d2), .C(C_t), .en(1'b1), .Q(IR_q));
  // decoder decoder_2: pin names not known; wires that end beside it: IR_q, C_t, decoder_2_p3, load, store, add, halt_t
  // Probe on decoder_2_p3
endmodule
